// Logisim project Lab_6_logisim.circ as structural Verilog: 2 circuits, main circuit main
module main (
  input  D,
  input  C,
  input  B,
  input  A
);

  wire n7447_1_pin9, n7447_1_pin10, n7447_1_pin11, n7447_1_pin12, n7447_1_pin13, n7447_1_pin14,
       n7447_1_pin15, not_1_out, not_2_out, not_3_out, not_4_out, not_5_out, not_6_out, not_7_out;

  _7447 #(.ShowInternalStructure("true")) u_7447_1 (
    .pin1(B), .pin2(C), .pin6(D), .pin7(A), .pin15(n7447_1_pin15), .pin14(n7447_1_pin14),
    .pin13(n7447_1_pin13), .pin12(n7447_1_pin12), .pin11(n7447_1_pin11), .pin10(n7447_1_pin10),
    .pin9(n7447_1_pin9));  // open: pin3, pin4, pin5
  not not_1 (not_1_out, n7447_1_pin14);
  not not_2 (not_2_out, n7447_1_pin15);
  not not_3 (not_3_out, n7447_1_pin13);
  not not_4 (not_4_out, n7447_1_pin12);
  not not_5 (not_5_out, n7447_1_pin11);
  not not_6 (not_6_out, n7447_1_pin10);
  not not_7 (not_7_out, n7447_1_pin9);
  _7_Segment_Display u_7_segment_display_1 (
    .g(not_1_out), .f(not_2_out), .a(not_3_out), .b(not_4_out), .e(not_7_out), .d(not_6_out), .c(not_5_out));  // open: dp
endmodule

module bcd_to_7_seg (
  input  in_1,
  input  in_2,
  input  B,
  input  in_4,
  output a,
  output out_6,
  output c,
  output d,
  output e,
  output f,
  output g
);

  wire and_1_out, and_2_out, and_3_out, and_4_out, and_5_out, and_6_out, and_7_out, and_8_out, and_9_out,
       and_10_out, and_11_out, and_12_out, and_13_out, and_14_out, and_15_out, and_16_out, not_1_out,
       not_2_out, not_3_out;

  not not_1 (not_1_out, in_2);
  not not_2 (not_2_out, B);
  not not_3 (not_3_out, in_4);
  and and_1 (and_1_out, not_1_out, not_3_out);
  and and_2 (and_2_out, in_2, in_4);
  and and_3 (and_3_out, not_2_out, not_3_out);
  and and_4 (and_4_out, B, in_4);
  or or_1 (c, not_2_out, in_4, in_2);
  and and_5 (and_5_out, not_1_out, not_3_out);
  and and_6 (and_6_out, not_1_out, B);
  and and_7 (and_7_out, in_2, not_2_out, in_4);
  and and_8 (and_8_out, B, not_3_out);
  and and_9 (and_9_out, not_1_out, not_3_out);
  and and_10 (and_10_out, B, not_3_out);
  and and_11 (and_11_out, not_2_out, not_3_out);
  and and_12 (and_12_out, in_2, not_2_out);
  and and_13 (and_13_out, in_2, not_3_out);
  and and_14 (and_14_out, not_1_out, B);
  and and_15 (and_15_out, in_2, not_2_out);
  and and_16 (and_16_out, B, not_3_out);
  or or_2 (a, and_1_out, B, and_2_out, in_1);
  or or_3 (out_6, not_1_out, and_3_out, and_4_out);
  or or_4 (d, and_5_out, and_6_out, and_7_out, and_8_out, in_1);
  or or_5 (e, and_9_out, and_10_out);
  or or_6 (f, and_11_out, and_12_out, and_13_out, in_1);
  or or_7 (g, and_14_out, and_15_out, in_1, and_16_out);
endmodule
