// Logisim project Lab_6_logisim_using_basic_gates.circ as structural Verilog: 2 circuits, main circuit main
module main (
  input  D,
  input  C,
  input  B,
  input  A
);

  wire and_1_out, and_2_out, and_3_out, and_4_out, and_5_out, and_6_out, and_7_out, and_8_out, and_9_out,
       and_10_out, not_1_out, not_2_out, not_3_out, or_1_out, or_2_out, or_3_out, or_4_out, or_5_out,
       or_6_out, or_7_out;

  not not_1 (not_1_out, C);
  not not_2 (not_2_out, B);
  not not_3 (not_3_out, A);
  and and_1 (and_1_out, A, C);
  and and_2 (and_2_out, not_3_out, not_1_out);
  and and_3 (and_3_out, A, B);
  and and_4 (and_4_out, not_3_out, not_2_out);
  and and_5 (and_5_out, B, not_1_out);
  and and_6 (and_6_out, A, not_2_out, C);
  and and_7 (and_7_out, not_3_out, B);
  and and_8 (and_8_out, not_2_out, C);
  and and_9 (and_9_out, not_3_out, C);
  and and_10 (and_10_out, not_3_out, B);
  or or_1 (or_1_out, and_1_out, and_2_out, B, D);
  or or_2 (or_2_out, and_3_out, and_4_out, not_1_out);
  or or_3 (or_3_out, not_2_out, A, C);
  or or_4 (or_4_out, and_2_out, and_5_out, and_7_out, and_6_out, D);
  or or_5 (or_5_out, and_7_out, and_2_out);
  or or_6 (or_6_out, and_4_out, and_8_out, and_9_out, D);
  or or_7 (or_7_out, and_5_out, and_8_out, and_10_out, D);
  _7_Segment_Display u_7_segment_display_1 (
    .g(or_7_out), .f(or_6_out), .a(or_1_out), .b(or_2_out), .e(or_5_out), .d(or_4_out), .c(or_3_out));  // open: dp

  // Notes on the sheet:
  //   BCD to 7 Segment Display using Basic Gates
  //   Id: 2312028042
  //   Name: Nabiha Nahin
endmodule

module vr (
  input  in_1,
  input  D,
  input  C,
  input  in_4
);

  wire and_1_out, and_2_out, and_3_out, and_4_out, and_5_out, and_6_out, and_7_out, and_8_out, and_9_out,
       and_10_out, and_11_out, and_12_out, and_13_out, and_14_out, and_15_out, and_16_out, not_1_out,
       not_2_out, not_3_out, or_1_out, or_2_out, or_3_out, or_4_out, or_5_out, or_6_out, or_7_out;

  not not_1 (not_1_out, C);
  not not_2 (not_2_out, in_1);
  not not_3 (not_3_out, in_4);
  and and_1 (and_1_out, not_1_out, not_3_out);
  and and_2 (and_2_out, C, in_4);
  and and_3 (and_3_out, not_2_out, not_3_out);
  and and_4 (and_4_out, in_1, in_4);
  or or_1 (or_1_out, not_2_out, in_4, C);
  and and_5 (and_5_out, not_1_out, not_3_out);
  and and_6 (and_6_out, not_1_out, in_1);
  and and_7 (and_7_out, C, not_2_out, in_4);
  and and_8 (and_8_out, in_1, not_3_out);
  and and_9 (and_9_out, not_1_out, not_3_out);
  and and_10 (and_10_out, in_1, not_3_out);
  and and_11 (and_11_out, not_2_out, not_3_out);
  and and_12 (and_12_out, C, not_2_out);
  and and_13 (and_13_out, C, not_3_out);
  and and_14 (and_14_out, not_1_out, in_1);
  and and_15 (and_15_out, C, not_2_out);
  and and_16 (and_16_out, in_1, not_3_out);
  or or_2 (or_2_out, and_1_out, in_1, and_2_out, D);
  or or_3 (or_3_out, not_1_out, and_3_out, and_4_out);
  or or_4 (or_4_out, and_5_out, and_6_out, and_7_out, and_8_out, D);
  or or_5 (or_5_out, and_9_out, and_10_out);
  or or_6 (or_6_out, and_11_out, and_12_out, and_13_out, D);
  or or_7 (or_7_out, and_14_out, and_15_out, D, and_16_out);
  _7_Segment_Display u_7_segment_display_1 (
    .g(or_7_out), .f(or_6_out), .a(or_2_out), .b(or_3_out), .e(or_5_out), .d(or_4_out), .c(or_1_out));  // open: dp
endmodule
