// Logisim project Assigment_1_D3.circ as structural Verilog: 1 circuit, main circuit main
module main (
  input  A,
  input  B,
  input  C,
  output F_I1_I2_I3
);

  wire and_1_out, and_2_out, and_3_out, not_1_out, not_2_out, or_1_out;

  not not_1 (not_1_out, A);
  not not_2 (not_2_out, B);
  and and_1 (and_1_out, not_1_out, C);
  and and_2 (and_2_out, A, not_2_out);
  and and_3 (and_3_out, B, C);
  or or_1 (or_1_out, and_1_out, and_2_out);
  or or_2 (F_I1_I2_I3, or_1_out, and_3_out);

  // Notes on the sheet:
  //   10
  //   1
  //   3
  //   2
  //   4
  //   6
  //   5
  //   9
  //   8
  //   I1=A'C
  //   I2=AB'
  //   I3=BC
  //   1
  //                        3
  //   2
  //   4
  //   5
  //   6
  //   F
endmodule
