// Logisim project Assignment_1_D2.circ as structural Verilog: 1 circuit, main circuit main
module main (
  input  A,
  input  B,
  input  C,
  input  _1,
  input  _2,
  input  C_2,
  output F_ABC,
  output F_A_B_C
);

  wire and_1_out, or_1_out;

  and and_1 (and_1_out, A, B);
  or or_1 (or_1_out, _1, _2);
  and and_2 (F_ABC, and_1_out, C);
  or or_2 (F_A_B_C, or_1_out, C_2);

  // Notes on the sheet:
  //   A
  //   B
  //   1
  //   2
  //   3
  //   3
  //   Extension of inputs of OR
  //   4
  //   AB
  //   5
  //   Extension of inputs of AND
  //   4
  //   A+B
  //   5
  //   6
  //   6
  //   F
  //   F
endmodule
