// Logisim project Lab2_Assignment_Canonical1_LogicGate.circ as structural Verilog: 1 circuit, main circuit main
module main (
  input  A,
  input  B,
  input  C,
  output out_4
);

  wire and_1_out, and_2_out, and_3_out, not_1_out, not_2_out, not_3_out;

  not not_1 (not_1_out, A);
  not not_2 (not_2_out, B);
  not not_3 (not_3_out, C);
  and and_1 (and_1_out, not_1_out, C);
  and and_2 (and_2_out, not_1_out, not_3_out);
  and and_3 (and_3_out, A, not_3_out);
  or or_1 (out_4, and_1_out, and_3_out);

  // Notes on the sheet:
  //   1
  //   2
  //   3
  //   4
  //   5
  //   6
  //   1
  //   2
  //   9
  //   8
  //   3
  //   4
  //   6
  //   5
  //   13
  //   12
  //   10
  //   11
  //   A'B'C
  //   A'BC'
  //   ABC'
  //   3
  //   4
  //   5
  //   6
  //   F(A,B,C)=A'B'C+A'BC'+ABC'
  //   Nabiha Nahin
endmodule
