// Logisim project Lab2_Assignment_Canonical2_IC.circ as structural Verilog: 1 circuit, main circuit main
module main (
  input  A,
  input  B,
  input  C,
  output out_4
);

  wire n7404_1_pin2, n7404_1_pin4, n7404_1_pin6, n7411_1_pin12, n7432_1_pin3, n7432_1_pin6, n7432_1_pin8,
       n7432_1_pin11, n7432_2_pin3, n7432_2_pin6, n7432_2_pin8, n7432_2_pin11, n7432_3_pin3, n7432_3_pin6;

  _7404 #(.ShowInternalStructure("true")) u_7404_1 (
    .pin1(A), .pin2(n7404_1_pin2), .pin3(B), .pin4(n7404_1_pin4), .pin5(C), .pin6(n7404_1_pin6));  // open: pin13, pin12, pin11, pin10, pin9, pin8
  _7432 #(.ShowInternalStructure("true")) u_7432_1 (
    .pin1(A), .pin2(B), .pin3(n7432_1_pin3), .pin4(n7432_1_pin3), .pin5(C), .pin6(n7432_1_pin6),
    .pin13(n7404_1_pin2), .pin12(B), .pin11(n7432_1_pin11), .pin10(n7432_1_pin11), .pin9(C),
    .pin8(n7432_1_pin8));
  _7432 #(.ShowInternalStructure("true")) u_7432_2 (
    .pin1(A), .pin2(n7404_1_pin4), .pin3(n7432_2_pin3), .pin4(n7432_2_pin3), .pin5(n7404_1_pin6),
    .pin6(n7432_2_pin6), .pin13(n7404_1_pin2), .pin12(B), .pin11(n7432_2_pin11), .pin10(n7432_2_pin11),
    .pin9(n7404_1_pin6), .pin8(n7432_2_pin8));
  _7432 #(.ShowInternalStructure("true")) u_7432_3 (
    .pin1(n7404_1_pin2), .pin2(n7404_1_pin4), .pin3(n7432_3_pin3), .pin4(n7432_3_pin3), .pin5(n7404_1_pin6),
    .pin6(n7432_3_pin6));  // open: pin13, pin12, pin11, pin10, pin9, pin8
  _7411 #(.ShowInternalStructure("true")) u_7411_1 (
    .pin1(n7432_1_pin6), .pin2(n7432_2_pin6), .pin13(n7432_1_pin8), .pin12(n7411_1_pin12),
    .pin11(n7411_1_pin12), .pin10(n7432_2_pin8), .pin9(n7432_3_pin6), .pin8(out_4));  // open: pin3, pin4, pin5, pin6

  // Notes on the sheet:
  //   A'
  //   B'
  //   C'
  //   (A'+B+C)
  //   (A+B+C)
  //   (A'+B'+C')
  //   (A'+B+C')
  //   (A+B'+C')
  //   F(A,B,C)=(A+B+C).(A+B'+C').(A'+B+C).(A'+B+C').(A'+B'+C')
  //   Nabiha Nahin
endmodule
