// Logisim project Lab2_Assignment_Canonical2_LogicGate.circ as structural Verilog: 1 circuit, main circuit main
module main (
  input  A,
  input  B,
  input  C,
  output out_4
);

  wire not_1_out, not_2_out, not_3_out, or_1_out, or_2_out, or_3_out, or_4_out, or_5_out;

  not not_1 (not_1_out, A);
  not not_2 (not_2_out, B);
  not not_3 (not_3_out, C);
  or or_1 (or_1_out, A, C);
  or or_2 (or_2_out, A, not_3_out);
  or or_3 (or_3_out, not_1_out, C);
  or or_4 (or_4_out, not_1_out, not_3_out);
  or or_5 (or_5_out, not_1_out, not_3_out);
  and and_1 (out_4, or_1_out, or_5_out);

  // Notes on the sheet:
  //   1
  //   2
  //   3
  //   4
  //   5
  //   6
  //   (A+B+C)
  //   (A+B'+C')
  //   (A'+B+C)
  //   (A'+B+C')
  //   (A'+B'+C')
  //   Nabiha Nahin
  //   F(A,B,C)=(A+B+C)*(A+B'+C')*(A'+B+C)*(A'+B+C')*(A'+B'+C')
endmodule
