// Logisim project Lab3_with_NOR.circ as structural Verilog: 1 circuit, main circuit main
module main (
  input  in_1,
  input  in_2,
  input  in_3,
  input  in_4,
  input  in_5,
  input  A,
  input  A_2,
  input  B,
  input  B_2,
  input  A_3,
  input  B_3,
  input  C,
  output \output ,
  output output_2,
  output output_3,
  output out_16,
  output out_17,
  output output_4
);

  wire n7402_2_pin1, n7402_2_pin4, n7402_2_pin10, n7402_2_pin13, n7402_3_pin1, n7402_3_pin4, n7402_3_pin10,
       n7402_3_pin13, n7402_5_pin1, n7402_6_pin1, n7402_6_pin3, n7402_7_pin1, n7402_7_pin4, n7402_8_pin1,
       n7402_8_pin4, n7402_8_pin13;

  _7402 #(.ShowInternalStructure("true")) u_7402_1 (
    .pin1(output_2), .pin2(in_2), .pin3(in_2));  // open: pin4, pin5, pin6, pin13, pin12, pin11, pin10, pin9, pin8
  _7402 #(.ShowInternalStructure("true")) u_7402_2 (
    .pin1(n7402_2_pin1), .pin2(A), .pin3(B_2), .pin4(n7402_2_pin4), .pin5(n7402_2_pin1), .pin6(A),
    .pin13(n7402_2_pin13), .pin12(n7402_2_pin1), .pin11(B_2), .pin10(n7402_2_pin10), .pin9(n7402_2_pin13),
    .pin8(n7402_2_pin4));
  _7402 #(.ShowInternalStructure("true")) u_7402_3 (
    .pin1(n7402_3_pin1), .pin2(A_3), .pin3(A_3), .pin4(n7402_3_pin4), .pin5(C), .pin6(C),
    .pin13(n7402_3_pin13), .pin12(n7402_3_pin1), .pin11(n7402_3_pin4), .pin10(n7402_3_pin10), .pin9(B_3),
    .pin8(B_3));
  _7402 #(.ShowInternalStructure("true")) u_7402_4 (
    .pin4(out_16), .pin5(n7402_2_pin10), .pin6(n7402_2_pin10));  // open: pin1, pin2, pin3, pin13, pin12, pin11, pin10, pin9, pin8
  _7402 #(.ShowInternalStructure("true")) u_7402_5 (
    .pin1(n7402_5_pin1), .pin2(in_1), .pin3(in_4), .pin4(output_3), .pin5(n7402_5_pin1), .pin6(n7402_5_pin1));  // open: pin13, pin12, pin11, pin10, pin9, pin8
  _7402 #(.ShowInternalStructure("true")) u_7402_6 (
    .pin1(n7402_6_pin1), .pin2(n7402_3_pin13), .pin3(n7402_6_pin3), .pin4(n7402_6_pin3), .pin5(C),
    .pin6(n7402_3_pin10), .pin13(output_4), .pin12(n7402_6_pin1), .pin11(n7402_6_pin1));  // open: pin10, pin9, pin8
  _7402 #(.ShowInternalStructure("true")) u_7402_7 (
    .pin1(n7402_7_pin1), .pin2(in_3), .pin3(in_3), .pin4(n7402_7_pin4), .pin5(in_5), .pin6(in_5),
    .pin13(\output ), .pin12(n7402_7_pin1), .pin11(n7402_7_pin4));  // open: pin10, pin9, pin8
  _7402 #(.ShowInternalStructure("true")) u_7402_8 (
    .pin1(n7402_8_pin1), .pin2(A_2), .pin3(B), .pin4(n7402_8_pin4), .pin5(n7402_8_pin1), .pin6(A_2),
    .pin13(n7402_8_pin13), .pin12(n7402_8_pin1), .pin11(B), .pin10(out_17), .pin9(n7402_8_pin13),
    .pin8(n7402_8_pin4));

  // Notes on the sheet:
  //   NOT
  //   XOR
  //   NOT,OR,AND,XOR,XNOR & Fig-B2 using NOR
  //   OR
  //   Figure-B2
  //   output
  //   AND
  //   XNOR
  //   output
endmodule
