// Logisim project Lab_3_with_NAND.circ as structural Verilog: 1 circuit, main circuit main
module main (
  input  in_1,
  input  in_2,
  input  in_3,
  input  in_4,
  input  in_5,
  input  in_6,
  input  in_7,
  input  in_8,
  input  in_9,
  input  A,
  input  B,
  input  C,
  output \output ,
  output output_2,
  output output_3,
  output output_4,
  output output_5,
  output out_18
);

  wire n7400_2_pin3, n7400_2_pin6, n7400_2_pin8, n7400_2_pin11, n7400_4_pin3, n7400_5_pin3, n7400_5_pin6,
       n7400_5_pin12, n7400_6_pin3, n7400_6_pin6, n7400_6_pin11, n7400_7_pin3, n7400_7_pin6, n7400_8_pin3;

  _7400 #(.ShowInternalStructure("true")) u_7400_1 (
    .pin1(in_1), .pin2(in_1), .pin3(\output ));  // open: pin4, pin5, pin6, pin13, pin12, pin11, pin10, pin9, pin8
  _7400 #(.ShowInternalStructure("true")) u_7400_2 (
    .pin1(in_6), .pin2(in_6), .pin3(n7400_2_pin3), .pin4(n7400_2_pin3), .pin5(in_9), .pin6(n7400_2_pin6),
    .pin13(in_9), .pin12(in_9), .pin11(n7400_2_pin11), .pin10(n7400_2_pin11), .pin9(in_6), .pin8(n7400_2_pin8));
  _7400 #(.ShowInternalStructure("true")) u_7400_3 (
    .pin4(n7400_2_pin8), .pin5(n7400_2_pin6), .pin6(output_5));  // open: pin1, pin2, pin3, pin13, pin12, pin11, pin10, pin9, pin8
  _7400 #(.ShowInternalStructure("true")) u_7400_4 (
    .pin1(in_3), .pin2(in_4), .pin3(n7400_4_pin3), .pin4(n7400_4_pin3), .pin5(n7400_4_pin3), .pin6(output_3));  // open: pin13, pin12, pin11, pin10, pin9, pin8
  _7400 #(.ShowInternalStructure("true")) u_7400_5 (
    .pin1(A), .pin2(C), .pin3(n7400_5_pin3), .pin4(C), .pin5(C), .pin6(n7400_5_pin6), .pin13(n7400_5_pin3),
    .pin12(n7400_5_pin12), .pin11(out_18), .pin10(B), .pin9(n7400_5_pin6), .pin8(n7400_5_pin12));
  _7400 #(.ShowInternalStructure("true")) u_7400_6 (
    .pin1(in_7), .pin2(in_7), .pin3(n7400_6_pin3), .pin4(in_8), .pin5(in_8), .pin6(n7400_6_pin6),
    .pin13(n7400_6_pin3), .pin12(n7400_6_pin6), .pin11(n7400_6_pin11));  // open: pin10, pin9, pin8
  _7400 #(.ShowInternalStructure("true")) u_7400_7 (
    .pin1(in_2), .pin2(in_2), .pin3(n7400_7_pin3), .pin4(in_5), .pin5(in_5), .pin6(n7400_7_pin6),
    .pin13(n7400_7_pin3), .pin12(n7400_7_pin6), .pin11(output_2));  // open: pin10, pin9, pin8
  _7400 #(.ShowInternalStructure("true")) u_7400_8 (
    .pin1(in_7), .pin2(in_8), .pin3(n7400_8_pin3), .pin4(n7400_6_pin11), .pin5(n7400_8_pin3), .pin6(output_4));  // open: pin13, pin12, pin11, pin10, pin9, pin8

  // Notes on the sheet:
  //   NOT
  //   XOR
  //   NOT,AND,OR,XOR,XNOR & Fig-B2 using NAND
  //   AND
  //   Figure-B2
  //   OR
  //   output
  //   XNOR
endmodule
