// Logisim project JK_flipflop.circ as structural Verilog: 1 circuit, main circuit main
module main (
  input  in_1,
  input  in_2,
  output out_3,
  output out_4
);

  wire and_1_out, and_2_out, clock_1_out;

  Clock clock_1 (.out(clock_1_out));
  D_Flip_Flop d_ff_1 ();  // open: D, clk, Q, Qn, preset, reset
  and and_1 (and_1_out, out_3, in_1, clock_1_out);
  and and_2 (and_2_out, clock_1_out, in_2, out_4);
  _7474 #(.ShowInternalStructure("true")) u_7474_1 ();  // open: pin1, pin2, pin3, pin4, pin5, pin6, pin13, pin12, pin11, pin10, pin9, pin8
  D_Flip_Flop d_ff_2 ();  // open: D, clk, Q, Qn, preset, reset
  nor nor_1 (out_3, and_1_out, out_4);
  nor nor_2 (out_4, out_3, and_2_out);
  D_Flip_Flop d_ff_3 ();  // open: D, clk, Q, Qn, preset, reset
  D_Flip_Flop d_ff_4 ();  // open: D, clk, Q, Qn, preset, reset
endmodule
